# Fritzing sketch EsquematicoCircuitoMatrizLED (saved by Fritzing 0.9.3b)
breadboards: 1

parts:
  Componente1 = Arduino Uno (Rev3)
  PSU1 = Adjustable Breadboard Power Supply  # not connected
  U1 = WS2812 RGB LED matrix 8x8
  R1 = Resistor [tolerance=±5% resistance=1k package=THT]

nets:
  N1: Componente1.D6_PWM, R1.Pin_0
  N2: U1.VCC, R1.Pin_1

custom parts:
  WS2812 RGB LED matrix 8x8: WS2812 matrix 8x8
